# Fritzing sketch shopping_cart (saved by Fritzing 0.9.3b)
breadboards: 1

parts:
  Componente1 = Arduino Nano (Rev3.0)
  J1 = Basic Servo
  U6 = LIPO-110mAh [package=lipo-110]
  U7 = L298_BRIDGE_DRIVER [package=powerso20]
  M1 = DC Motor
  U8 = ESP8266 WiFi Module [part_number=ESP8266]

nets:
  N1: Componente1.D1/TX, U8.RXD
  N2: Componente1.D0/RX, U8.TXD
  GND: Componente1.GND, J1.gnd, U6.-, U7.GND, U8.GND
  N3: Componente1.D2, J1.pulse
  N4: Componente1.D4, U7.IN1
  N5: Componente1.D5, U7.IN2
  N6: Componente1.VIN, U6.+, U7.VS
  VCC: Componente1.5V, J1.vcc, U8.VCC
  N7: U7.OUT1, M1.pin_2
  N8: U7.OUT2, M1.pin_1

custom parts:
  LIPO-110mAh: 110mAh Lipo-battery
